// Logisim project PRATICAL 1.circ as structural Verilog: 1 circuit, main circuit main
module main (
  input  A,
  input  A_2,
  input  in_3,
  input  in_4,
  input  Y_A_prime,
  input  A_3,
  input  in_7,
  input  A_4,
  input  B,
  input  B_2,
  input  B_3,
  input  A_5,
  input  B_4,
  output Y_A_B,
  output out_15,
  output Y_A_B_2,
  output Y__A_B__prime,
  output Y__A_B,
  output out_19,
  output out_20
);

  and and_1 (Y_A_B, A, in_4);
  nand nand_1 (Y__A_B__prime, A_3, B);
  xnor xnor_1 (out_20, A_5, B_4);
  not not_1 (out_15, A_2);
  nor nor_1 (Y__A_B, A_4, B_2);
  or or_1 (Y_A_B_2, in_3, Y_A_prime);
  xor xor_1 (out_19, in_7, B_3);

  // Notes on the sheet:
  //   B
  //   AND GATE
  //   NAND GATE
  //   XNOR GATE
  //   Y=(AB'+A'B)
  //   NOT GATE
  //   NOR GATE
  //   A
  //   B
  //   OR GATE
  //   A
  //   XOR GATE
  //   Y=AB'+A'B
endmodule
